# Fritzing sketch Fritzing (saved by Fritzing 0.9.3b)
breadboards: 1

parts:
  R1 = Resistor [tolerance=±5% resistance=100 package=THT]
  R3 = Resistor [tolerance=±5% resistance=21 package=THT]
  Q1 = NPN-Transistor [package="TO92 [THT]"]
  Adafruit_HUZZAH_ESP8266_Breakout1 = Adafruit HUZZAH ESP8266 Breakout [part_number=2471]

nets:
  N1: R1.Pin_0, Adafruit_HUZZAH_ESP8266_Breakout1.V+
  N2: R1.Pin_1, Q1.E
  N3: R3.Pin_0, Adafruit_HUZZAH_ESP8266_Breakout1.#5
  N4: R3.Pin_1, Q1.B
  N5: Q1.C, Adafruit_HUZZAH_ESP8266_Breakout1.GND
